# Fritzing sketch esp-desk-util (saved by Fritzing 0.9.5d)

parts:
  esp1 = ESP32 DevKitc V4
  A1 = DHT22 module
  AHT1 = AHT20 BMP280 pressure and humidity breakout
  OLED_I2C1 = OLED 128x64 I2C Monochrome Display
  Sensor1 = TTP223B Capacitive Touch Sensor Module
  J1 = male pin header, 5 pins [form="♂ (male)"]
  RGB_SMD_LED1 = SMD RGB LED (WS2812) [package=5050]
  J2 = male pin header, 6 pins [form="♂ (male)"]

nets:
  N1: esp1.IO16, OLED_I2C1.SDA
  N2: esp1.IO17, OLED_I2C1.SCK
  N3: esp1.IO18, AHT1.SDA
  N4: esp1.IO19, AHT1.SCL
  N5: esp1.IO21, Sensor1.SIG
  N6: esp1.IO22, RGB_SMD_LED1.DIn
  N7: esp1.3V3, J1.pin1
  N8: esp1.GND, J2.pin1
  N9: esp1.IO13, A1.DAT
  N10: A1.GND, J2.pin2
  N11: A1.VCC, J1.pin2
  N12: AHT1.VDD, J1.pin3
  N13: AHT1.GND, J2.pin3
  N14: OLED_I2C1.VDD, J1.pin4
  N15: OLED_I2C1.GND, J2.pin4
  N16: Sensor1.GND, J2.pin5
  N17: Sensor1.VCC, J1.pin5
  N18: RGB_SMD_LED1.VSS, J2.pin6

custom parts:
  ESP32 DevKitc V4: ESP32-DevKitC board with ESP32-WROOM-32 module. ESP32-DevKitC V4 is a small-sized ESP32-based development board produced by Espressif. Most of the pins on the ESP module are broken out to the pin headers on the board. The pins D0, D1, D2, D3, CMD and CLK are used internally for communication between ESP32 and SPI flash memory. They are grouped on both sides near the USB connector. Avoid using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
  DHT22 module: DHT22 module. Pins GND VCC Data.
  AHT20 BMP280 pressure and humidity breakout: Cheap breakout board for the BMP280, barometric pressure sensor, and AHT20, humidity sensor
  TTP223B Capacitive Touch Sensor Module: The TTP223B capacitive touch sensor module uses the TTP223B IC. The appropriate voltage is approximately 2 to 5.5 volts.
